// Logisim project atividade_arquitetura.circ as structural Verilog: 5 circuits, main circuit main
module main (
  input  in_1,
  input  in_2,
  input  in_3,
  input  in_4,
  input  in_5,
  input  in_6
);

  wire clock_1_out, somador_3_bits_1_out_7, somador_3_bits_1_out_8, somador_3_bits_1_out_9;

  somador_3_bits somador_3_bits_1 (
    .in_1(in_3), .in_2(in_1), .in_3(in_5), .in_4(in_2), .in_5(in_4), .in_6(in_6),
    .out_7(somador_3_bits_1_out_7), .out_9(somador_3_bits_1_out_9), .out_8(somador_3_bits_1_out_8));  // open: out_10
  Clock clock_1 (.out(clock_1_out));
  registrador_3_bits registrador_3_bits_1 (
    .in_1(clock_1_out), .in_2(somador_3_bits_1_out_8), .in_3(somador_3_bits_1_out_9),
    .in_4(somador_3_bits_1_out_7));  // open: out_5, out_6, out_7
endmodule

module registrador_3_bits (
  input  in_1,
  input  in_2,
  input  in_3,
  input  in_4,
  output out_5,
  output out_6,
  output out_7
);

  wire undriven;

  D_Flip_Flop d_ff_1 (.clk(undriven), .D(in_4), .Q(out_7));  // open: Qn, preset, en, reset
  D_Flip_Flop d_ff_2 (.clk(undriven), .D(in_2), .Q(out_5));  // open: Qn, preset, en, reset
  D_Flip_Flop d_ff_3 (.clk(undriven), .D(in_3), .Q(out_6));  // open: Qn, preset, en, reset
endmodule

module somador_3_bits (
  input  in_1,
  input  in_2,
  input  in_3,
  input  in_4,
  input  in_5,
  input  in_6,
  output out_7,
  output out_8,
  output out_9,
  output out_10
);

  wire meio_somador_1_out_4, somador_completo_1_out_5;

  meio_somador meio_somador_1 (.in_1(in_4), .in_2(in_2), .out_3(out_7), .out_4(meio_somador_1_out_4));
  somador_completo somador_completo_1 (
    .in_1(in_5), .in_2(in_1), .in_3(meio_somador_1_out_4), .out_4(out_9), .out_5(somador_completo_1_out_5));
  somador_completo somador_completo_2 (
    .in_1(in_6), .in_2(in_3), .in_3(somador_completo_1_out_5), .out_4(out_8), .out_5(out_10));
endmodule

module meio_somador (
  input  in_1,
  input  in_2,
  output out_3,
  output out_4
);

  xor xor_1 (out_3, in_1, in_2);
  and and_1 (out_4, in_1, in_2);
endmodule

module somador_completo (
  input  in_1,
  input  in_2,
  input  in_3,
  output out_4,
  output out_5
);

  wire and_1_out, and_2_out, and_3_out, xor_1_out;

  xor xor_1 (xor_1_out, in_1, in_2);
  and and_1 (and_1_out, in_2, in_3);
  and and_2 (and_2_out, in_1, in_3);
  and and_3 (and_3_out, in_2, in_1);
  xor xor_2 (out_4, xor_1_out, in_3);
  or or_1 (out_5, and_1_out, and_2_out, and_3_out);
endmodule
